// Digital circuit cpu.dig as structural Verilog
module cpu (
  input  clk,
  output [31:0] Current_instruction,
  output [31:0] PC,
  output [31:0] RS1,
  output [31:0] RS2,
  output [4:0] RSA,
  output [31:0] Lau_out,
  output [31:0] Mem_in,
  output [31:0] RDA,
  output Store_register,
  output Store_memory,
  output Load_lau,
  output Load_IMM,
  output Load_PC
);

  wire and_1_out, lau_1_zero, not_1_out, pc_signal_1_pc_alu, pc_signal_1_plus__imm;
  wire [2:0] signal_proc_1_func_3;
  wire [6:0] signal_proc_1_func_7;
  wire [31:0] add_1_s, data_d, imm_proc_1_imm, multiplexer_1_out, multiplexer_2_out, multiplexer_5_out;

  pc_signal pc_signal_1 (
    .Opcode(Current_instruction[6:0]), .Func_3(signal_proc_1_func_3), .Alu_out(Lau_out),
    .Zero_out(lau_1_zero), .PC_Alu(pc_signal_1_pc_alu), .plus__IMM(pc_signal_1_plus__imm));
  Multiplexer #(.Bits(32)) multiplexer_1 (
    .sel(pc_signal_1_plus__imm), .in_0(32'h4), .in_1(imm_proc_1_imm), .out(multiplexer_1_out));
  Add #(.Bits(32)) add_1 (.a(PC), .b(multiplexer_1_out), .c_i(1'b0), .s(add_1_s));  // open: c_o
  Multiplexer #(.Bits(32)) multiplexer_2 (
    .sel(pc_signal_1_pc_alu), .in_0(add_1_s), .in_1(Lau_out), .out(multiplexer_2_out));
  and and_1 (and_1_out, Current_instruction[0], Current_instruction[1]);
  Register #(.Bits(32), .isProgramCounter("true")) u_PC (.D(multiplexer_2_out), .C(clk), .en(and_1_out), .Q(PC));
  rom text (.A(PC), .sel(1'b1), .D(Current_instruction));
  imm_proc imm_proc_1 (.Instruction(Current_instruction), .IMM(imm_proc_1_imm));
  signal_proc signal_proc_1 (
    .Opcode(Current_instruction[6:0]), .Rem(Current_instruction[31:12]), .Func_7(signal_proc_1_func_7),
    .Func_3(signal_proc_1_func_3), .Reg_Store(Store_register), .Mem_Store(Store_memory), .Load_Lau(Load_lau),
    .Lau_IMM(Load_IMM), .Load_PC(Load_PC));
  register_bank register_bank_1 (
    .RS1i(Current_instruction[19:15]), .RS2i(Current_instruction[24:20]), .RSA(Current_instruction[11:7]),
    .CLK(clk), .RDA(RDA), .WR(Store_register), .RS1(RS1), .RS2(RS2));
  Multiplexer #(.Bits(32)) multiplexer_3 (.sel(Load_IMM), .in_0(RS2), .in_1(imm_proc_1_imm), .out(Mem_in));
  lau lau_1 (
    .A(RS1), .B(Mem_in), .OP3(signal_proc_1_func_3), .OP7(signal_proc_1_func_7), .R(Lau_out),
    .Zero(lau_1_zero));
  Multiplexer #(.Bits(32)) multiplexer_4 (.sel(Load_PC), .in_0(multiplexer_5_out), .in_1(add_1_s), .out(RDA));
  Multiplexer #(.Bits(32)) multiplexer_5 (.sel(Load_lau), .in_0(data_d), .in_1(Lau_out), .out(multiplexer_5_out));
  ram data (.A(Lau_out), .Din(Mem_in), .str(Store_memory), .clk(clk), .ld(not_1_out), .D(data_d));
  not not_1 (not_1_out, Store_memory);

  assign RSA = Current_instruction[11:7];

  // Other names for the same wires on the sheet: ci[31:0] = Current_instruction; lau[31:0] = Lau_out; lc = Load_PC;
  //   li = Load_IMM; ll = Load_lau; mem[31:0] = Mem_in; ms = Store_memory; rs = Store_register

  // Notes on the sheet:
  //   Halter
  //   Debug values
  //   Debug flags
  //   Imm
endmodule
