// Digital circuit lau.dig as structural Verilog
module lau (
  input  [31:0] A,
  input  [31:0] B,
  input  [2:0] OP3,
  input  [6:0] OP7,
  output [31:0] R
);

  wire and_1_out, and_2_out, and_3_out, multiplexer_2_out;
  wire [31:0] add_1_s, and_4_out, barrelshifter_1_out, multiplexer_1_out, not_1_out, or_1_out, xor_1_out;

  and and_1 (and_1_out, OP7[6], ~OP3[0]);  // And
  and and_2 (and_2_out, OP3[1], ~OP3[2]);  // And
  and and_3 (and_3_out, and_1_out, and_2_out);
  not not_1 (not_1_out[0], B[0]);
  Multiplexer #(.Bits(32)) multiplexer_1 (.sel(and_3_out), .in_0(B), .in_1(not_1_out), .out(multiplexer_1_out));
  Multiplexer multiplexer_2 (.sel(and_3_out), .in_0(1'b0), .in_1(1'b1), .out(multiplexer_2_out));
  Add #(.Bits(32)) add_1 (.a(A), .b(multiplexer_1_out), .c_i(multiplexer_2_out), .s(add_1_s));  // open: c_o
  BarrelShifter #(.Bits(32), .barrelSigned("true")) barrelshifter_1 (.in(A), .shift(B[6:0]), .out(barrelshifter_1_out));
  assign xor_1_out = A ^ B;  // XOr xor_1, 32 bits wide
  assign or_1_out = A | B;  // Or or_1, 32 bits wide
  assign and_4_out = A & B;  // And and_4, 32 bits wide
  Multiplexer #(.Selector_Bits(3), .Bits(32)) multiplexer_3 (
    .sel(OP3), .in_0(add_1_s), .in_1(barrelshifter_1_out), .in_2(add_1_s), .in_3({32{1'b0}}),
    .in_4(xor_1_out), .in_5({32{1'b0}}), .in_6(or_1_out), .in_7(and_4_out), .out(R));
  // Pins of 1 and 32 bits meet at B
  // Pins of 1 and 32 bits meet at not_1_out
endmodule
