// Digital circuit ram.dig as structural Verilog
module ram (
  input  [31:0] A,
  input  [31:0] Din,
  input  str,
  input  clk,
  input  ld,
  output [31:0] D
);

  RAMDualPort #(.AddrBits(24), .Bits(8)) ramdualport_1 (
    .A(A[23:0]), .Din(Din[7:0]), .str(str), .C(clk), .ld(ld), .D(D[7:0]));
  RAMDualPort #(.AddrBits(24), .Bits(8)) ramdualport_2 (
    .A(A[23:0]), .Din(Din[15:8]), .str(str), .C(clk), .ld(ld), .D(D[15:8]));
  RAMDualPort #(.AddrBits(24), .Bits(8)) ramdualport_3 (
    .A(A[23:0]), .Din(Din[23:16]), .str(str), .C(clk), .ld(ld), .D(D[23:16]));
  RAMDualPort #(.AddrBits(24), .Bits(8)) ramdualport_4 (
    .A(A[23:0]), .Din(Din[31:24]), .str(str), .C(clk), .ld(ld), .D(D[31:24]));
endmodule
