// Digital circuit register-bank.dig as structural Verilog
module register_bank (
  input  [4:0] RS1i,
  input  [4:0] RS2i,
  input  [4:0] RSA,
  input  CLK,
  input  [31:0] RDA,
  input  WR,
  output [31:0] RS1,
  output [31:0] RS2
);

  wire demultiplexer_1_out_1, demultiplexer_1_out_2, demultiplexer_1_out_3, demultiplexer_1_out_4,
       demultiplexer_1_out_5, demultiplexer_1_out_6, demultiplexer_1_out_7, demultiplexer_1_out_8,
       demultiplexer_1_out_9, demultiplexer_1_out_10, demultiplexer_1_out_11, demultiplexer_1_out_12,
       demultiplexer_1_out_13, demultiplexer_1_out_14, demultiplexer_1_out_15, demultiplexer_1_out_16,
       demultiplexer_1_out_17, demultiplexer_1_out_18, demultiplexer_1_out_19, demultiplexer_1_out_20,
       demultiplexer_1_out_21, demultiplexer_1_out_22, demultiplexer_1_out_23, demultiplexer_1_out_24,
       demultiplexer_1_out_25, demultiplexer_1_out_26, demultiplexer_1_out_27, demultiplexer_1_out_28,
       demultiplexer_1_out_29, demultiplexer_1_out_30, demultiplexer_1_out_31;
  wire [31:0] register_1_q, register_2_q, register_3_q, register_4_q, register_5_q, register_6_q,
       register_7_q, register_8_q, register_9_q, register_10_q, register_11_q, register_12_q, register_13_q,
       register_14_q, register_15_q, register_16_q, register_17_q, register_18_q, register_19_q,
       register_20_q, register_21_q, register_22_q, register_23_q, register_24_q, register_25_q,
       register_26_q, register_27_q, register_28_q, register_29_q, register_30_q, register_31_q;

  Demultiplexer #(.Selector_Bits(5)) demultiplexer_1 (
    .sel(RSA), .in(WR), .out_1(demultiplexer_1_out_1), .out_2(demultiplexer_1_out_2),
    .out_3(demultiplexer_1_out_3), .out_4(demultiplexer_1_out_4), .out_5(demultiplexer_1_out_5),
    .out_6(demultiplexer_1_out_6), .out_7(demultiplexer_1_out_7), .out_8(demultiplexer_1_out_8),
    .out_9(demultiplexer_1_out_9), .out_10(demultiplexer_1_out_10), .out_11(demultiplexer_1_out_11),
    .out_12(demultiplexer_1_out_12), .out_13(demultiplexer_1_out_13), .out_14(demultiplexer_1_out_14),
    .out_15(demultiplexer_1_out_15), .out_16(demultiplexer_1_out_16), .out_17(demultiplexer_1_out_17),
    .out_18(demultiplexer_1_out_18), .out_19(demultiplexer_1_out_19), .out_20(demultiplexer_1_out_20),
    .out_21(demultiplexer_1_out_21), .out_22(demultiplexer_1_out_22), .out_23(demultiplexer_1_out_23),
    .out_24(demultiplexer_1_out_24), .out_25(demultiplexer_1_out_25), .out_26(demultiplexer_1_out_26),
    .out_27(demultiplexer_1_out_27), .out_28(demultiplexer_1_out_28), .out_29(demultiplexer_1_out_29),
    .out_30(demultiplexer_1_out_30), .out_31(demultiplexer_1_out_31));  // open: out_0
  Register #(.Bits(32)) register_1 (.D(RDA), .C(CLK), .en(demultiplexer_1_out_1), .Q(register_1_q));
  Register #(.Bits(32)) register_2 (.D(RDA), .C(CLK), .en(demultiplexer_1_out_2), .Q(register_2_q));
  Register #(.Bits(32)) register_3 (.D(RDA), .C(CLK), .en(demultiplexer_1_out_3), .Q(register_3_q));
  Register #(.Bits(32)) register_4 (.D(RDA), .C(CLK), .en(demultiplexer_1_out_4), .Q(register_4_q));
  Register #(.Bits(32)) register_5 (.D(RDA), .C(CLK), .en(demultiplexer_1_out_5), .Q(register_5_q));
  Register #(.Bits(32)) register_6 (.D(RDA), .C(CLK), .en(demultiplexer_1_out_6), .Q(register_6_q));
  Register #(.Bits(32)) register_7 (.D(RDA), .C(CLK), .en(demultiplexer_1_out_7), .Q(register_7_q));
  Register #(.Bits(32)) register_8 (.D(RDA), .C(CLK), .en(demultiplexer_1_out_8), .Q(register_8_q));
  Register #(.Bits(32)) register_9 (.D(RDA), .C(CLK), .en(demultiplexer_1_out_9), .Q(register_9_q));
  Register #(.Bits(32)) register_10 (.D(RDA), .C(CLK), .en(demultiplexer_1_out_10), .Q(register_10_q));
  Register #(.Bits(32)) register_11 (.D(RDA), .C(CLK), .en(demultiplexer_1_out_11), .Q(register_11_q));
  Register #(.Bits(32)) register_12 (.D(RDA), .C(CLK), .en(demultiplexer_1_out_12), .Q(register_12_q));
  Register #(.Bits(32)) register_13 (.D(RDA), .C(CLK), .en(demultiplexer_1_out_13), .Q(register_13_q));
  Register #(.Bits(32)) register_14 (.D(RDA), .C(CLK), .en(demultiplexer_1_out_14), .Q(register_14_q));
  Register #(.Bits(32)) register_15 (.D(RDA), .C(CLK), .en(demultiplexer_1_out_15), .Q(register_15_q));
  Register #(.Bits(32)) register_16 (.D(RDA), .C(CLK), .en(demultiplexer_1_out_16), .Q(register_16_q));
  Register #(.Bits(32)) register_17 (.D(RDA), .C(CLK), .en(demultiplexer_1_out_17), .Q(register_17_q));
  Register #(.Bits(32)) register_18 (.D(RDA), .C(CLK), .en(demultiplexer_1_out_18), .Q(register_18_q));
  Register #(.Bits(32)) register_19 (.D(RDA), .C(CLK), .en(demultiplexer_1_out_19), .Q(register_19_q));
  Register #(.Bits(32)) register_20 (.D(RDA), .C(CLK), .en(demultiplexer_1_out_20), .Q(register_20_q));
  Register #(.Bits(32)) register_21 (.D(RDA), .C(CLK), .en(demultiplexer_1_out_21), .Q(register_21_q));
  Register #(.Bits(32)) register_22 (.D(RDA), .C(CLK), .en(demultiplexer_1_out_22), .Q(register_22_q));
  Register #(.Bits(32)) register_23 (.D(RDA), .C(CLK), .en(demultiplexer_1_out_23), .Q(register_23_q));
  Register #(.Bits(32)) register_24 (.D(RDA), .C(CLK), .en(demultiplexer_1_out_24), .Q(register_24_q));
  Register #(.Bits(32)) register_25 (.D(RDA), .C(CLK), .en(demultiplexer_1_out_25), .Q(register_25_q));
  Register #(.Bits(32)) register_26 (.D(RDA), .C(CLK), .en(demultiplexer_1_out_26), .Q(register_26_q));
  Register #(.Bits(32)) register_27 (.D(RDA), .C(CLK), .en(demultiplexer_1_out_27), .Q(register_27_q));
  Register #(.Bits(32)) register_28 (.D(RDA), .C(CLK), .en(demultiplexer_1_out_28), .Q(register_28_q));
  Register #(.Bits(32)) register_29 (.D(RDA), .C(CLK), .en(demultiplexer_1_out_29), .Q(register_29_q));
  Register #(.Bits(32)) register_30 (.D(RDA), .C(CLK), .en(demultiplexer_1_out_30), .Q(register_30_q));
  Register #(.Bits(32)) register_31 (.D(RDA), .C(CLK), .en(demultiplexer_1_out_31), .Q(register_31_q));
  Multiplexer #(.Selector_Bits(5), .Bits(32)) multiplexer_1 (
    .sel(RS2i), .in_0({32{1'b0}}), .in_1(register_1_q), .in_2(register_2_q), .in_3(register_3_q),
    .in_4(register_4_q), .in_5(register_5_q), .in_6(register_6_q), .in_7(register_7_q), .in_8(register_8_q),
    .in_9(register_9_q), .in_10(register_10_q), .in_11(register_11_q), .in_12(register_12_q),
    .in_13(register_13_q), .in_14(register_14_q), .in_15(register_15_q), .in_16(register_16_q),
    .in_17(register_17_q), .in_18(register_18_q), .in_19(register_19_q), .in_20(register_20_q),
    .in_21(register_21_q), .in_22(register_22_q), .in_23(register_23_q), .in_24(register_24_q),
    .in_25(register_25_q), .in_26(register_26_q), .in_27(register_27_q), .in_28(register_28_q),
    .in_29(register_29_q), .in_30(register_30_q), .in_31(register_31_q), .out(RS2));
  Multiplexer #(.Selector_Bits(5), .Bits(32)) multiplexer_2 (
    .sel(RS1i), .in_0({32{1'b0}}), .in_1(register_1_q), .in_2(register_2_q), .in_3(register_3_q),
    .in_4(register_4_q), .in_5(register_5_q), .in_6(register_6_q), .in_7(register_7_q), .in_8(register_8_q),
    .in_9(register_9_q), .in_10(register_10_q), .in_11(register_11_q), .in_12(register_12_q),
    .in_13(register_13_q), .in_14(register_14_q), .in_15(register_15_q), .in_16(register_16_q),
    .in_17(register_17_q), .in_18(register_18_q), .in_19(register_19_q), .in_20(register_20_q),
    .in_21(register_21_q), .in_22(register_22_q), .in_23(register_23_q), .in_24(register_24_q),
    .in_25(register_25_q), .in_26(register_26_q), .in_27(register_27_q), .in_28(register_28_q),
    .in_29(register_29_q), .in_30(register_30_q), .in_31(register_31_q), .out(RS1));
endmodule
