// Digital circuit rom.dig as structural Verilog
module rom (
  input  [31:0] A,
  input  sel,
  output [31:0] D
);

  ROM #(.AddrBits(24), .Bits(8)) rom_1 (.A(A[23:0]), .sel(sel), .D(D[7:0]));
  ROM #(.AddrBits(24), .Bits(8)) rom_2 (.A(A[23:0]), .sel(sel), .D(D[15:8]));
  ROM #(.AddrBits(24), .Bits(8)) rom_3 (.A(A[23:0]), .sel(sel), .D(D[23:16]));
  ROM #(.AddrBits(24), .Bits(8)) rom_4 (.A(A[23:0]), .sel(sel), .D(D[31:24]));
endmodule
